# Fritzing sketch hardware (saved by Fritzing 0.9.3b)

parts:
  MCU1 = Raspberry Pi Zero
  hc-sr1 = hc-sr04
  R2 = Resistor [tolerance=±5% resistance=2k package="0805 [SMD]"]
  U1 = L298 [package=multiwatt15]
  M1 = DC Motor
  M2 = DC Motor
  VCC1 = 4 x AAA Battery Mount
  U2 = LIPO-2000mAh [package=lipo-2000]
  Part1 = Triple Axis Accelerometer Breakout - ADXL345
  U3 = TRANSCHIPTC5747 [package=camera_sfv24r-2st_2]  # not connected
  R1 = Resistor [tolerance=±5% resistance=1k package=THT]
  U4 = SUP500F [package=sup500f]

nets:
  N1: MCU1.pin_1, MCU1.pin_17, Part1.VCC
  VCC: MCU1.pin_2, MCU1.pin_4, hc-sr1.VCC, U2.+, U4.VCC
  N2: MCU1.pin_3, Part1.SDO, Part1.SDA
  N3: MCU1.pin_5, Part1.SCL
  GND: MCU1.pin_6, MCU1.pin_9, MCU1.pin_34, MCU1.pin_39, hc-sr1.GND, R2.Pin_1, U2.-, Part1.GND, U4.GND
  N4: MCU1.pin_8, U4.RX-I
  N5: MCU1.pin_10, U4.TX-O
  N6: MCU1.pin_31, hc-sr1.Trig
  N7: MCU1.pin_32, R2.Pin_0, R1.Pin_1
  N8: MCU1.pin_35, U1.IN2
  N9: MCU1.pin_36, U1.IN1, U1.ENA
  N10: MCU1.pin_37, U1.ENB, U1.IN4
  N11: MCU1.pin_38, U1.VLS, U1.IN3
  N12: hc-sr1.Echo, R1.Pin_0
  N13: U1.OUT1, M2.pin_2
  N14: U1.OUT2, M2.pin_1
  N15: U1.VS, VCC1.+
  N16: U1.GND, VCC1.-
  N17: U1.OUT3, M1.pin_2
  N18: U1.OUT4, M1.pin_1

notes:
  Pi Camera v2
  connected through
  Ribbon Cable
